// Logisim project CPU-final.circ as structural Verilog: 13 circuits, main circuit main
module main (
  input  clr
);

  wire alu_1_equal, alu_1_gt, CLK, clock_1_out, comparator_1_eq, comparator_2_eq, display, ex_mem_1_equal_2,
       ex_mem_1_gt_2, Halt, load_use, multiplexer_2_out, multiplexer_3_out, not_1_out, not_2_out, RegWrite;
  wire [1:0] Ex_Mem_Rd, Forword1, Forword2, id_ex_1_rd_2, id_ex_1_rs_2, id_ex_1_rt_2, ir_1_rs, ir_1_rt,
       mem_wr_1_regdst_2, multiplexer_4_out, PCSrc, Rd;
  wire [2:0] funct;
  wire [3:0] ALUOp, id_ex_1_aluop_2, op;
  wire [6:0] mem_wr_1_control_2;
  wire [7:0] id_ex_1_imm_offset_2, imm;
  wire [11:0] id_ex_1_jaddr_2, jAddr;
  wire [12:0] control_1_signextend__0;
  wire [12:1] ex_mem_1_control_2;
  wire [15:0] adder_2_out, alu_1_aluout, BranchAddr, CLKCounter, Control, controlled_buffer_1_out,
       controlled_buffer_2_out, d0, d1, ex_mem_1_aluout_2, ex_mem_1_rd2_2, id_ex_1_control_2, id_ex_1_rd1_2,
       id_ex_1_rd2_2, if_id_1_instruction_2, JumpAddr, mem_wr_1_aluout_2, mem_wr_1_memout_2,
       multiplexer_1_out, multiplexer_5_out, multiplexer_6_out, multiplexer_7_out, multiplexer_8_out, PC1,
       PC2, PC3, PC4, PC5, R_rs, R_rt, RAMValue, register_1_q, rg0, rg1, rg2, rg3, rom_1_data,
       signextend_1_extended_imm_offset;

  Multiplexer #(.select(2), .width(16), .enable("false")) multiplexer_1 (
    .in0(PC1), .in1(BranchAddr), .in2(JumpAddr), .out(multiplexer_1_out), .sel(PCSrc));  // open: in3
  Register #(.width(16)) register_1 (.D(multiplexer_1_out), .en(1'b1), .Q(register_1_q), .clk(CLK), .clr(clr));
  Counter #(.width(16), .max('hffff), .ongoal("continue")) counter_1 (
    .count(1'b1), .Q(CLKCounter), .clk(CLK), .clr(clr));  // open: load, D, carry
  and and_1 (CLK, clock_1_out, not_1_out);
  not not_1 (not_1_out, Halt);
  Clock clock_1 (.out(clock_1_out));
  Adder #(.width(16)) adder_1 (.a(16'h1), .b(register_1_q), .out(PC1));  // open: cin, cout
  // Probe on register_1_q
  Multiplexer #(.enable("false")) multiplexer_2 (
    .in0(display), .in1(1'b0), .out(multiplexer_2_out), .sel(comparator_1_eq));
  Comparator comparator_1 (.a(8'h1), .b(imm), .eq(comparator_1_eq));  // open: gt, lt
  Multiplexer #(.enable("false")) multiplexer_3 (
    .in0(display), .in1(1'b0), .out(multiplexer_3_out), .sel(comparator_2_eq));
  Comparator comparator_2 (.a({8{1'b0}}), .b(imm), .eq(comparator_2_eq));  // open: gt, lt
  Control control_1 (
    .op(op), .func(funct), .beq_4(control_1_signextend__0[4]), .aluSource_2(control_1_signextend__0[2]),
    .memToReg_9(control_1_signextend__0[9]), .bne_5(control_1_signextend__0[5]),
    .memRead_8(control_1_signextend__0[8]), .bgt_6(control_1_signextend__0[6]),
    .display_11(control_1_signextend__0[11]), .Jump_3(control_1_signextend__0[3]),
    .regWrite_10(control_1_signextend__0[10]), .signExtend__0(control_1_signextend__0[0]),
    .RegDst_1(control_1_signextend__0[1]), .halt_12(control_1_signextend__0[12]), .Control(Control),
    .aluFunc(ALUOp), .memWrite_7(control_1_signextend__0[7]));
  // Probe on Control
  Hex_Digit_Display hex_digit_display_1 (.value(d0[15:12]));  // open: dp
  Register #(.width(16)) register_2 (.D(R_rs), .en(multiplexer_2_out), .Q(d0), .clk(CLK), .clr(1'b0));
  Register #(.width(16)) register_3 (.D(R_rs), .en(multiplexer_3_out), .Q(d1), .clk(CLK), .clr(1'b0));
  ROM #(.addrWidth(16), .dataWidth(16)) rom_1 (.addr(register_1_q), .data(rom_1_data), .sel(1'b1));
  Hex_Digit_Display hex_digit_display_2 (.value(d0[11:8]));  // open: dp
  Hex_Digit_Display hex_digit_display_3 (.value(d0[7:4]));  // open: dp
  Hex_Digit_Display hex_digit_display_4 (.value(d1[15:12]));  // open: dp
  Hex_Digit_Display hex_digit_display_5 (.value(d1[11:8]));  // open: dp
  // Probe on {3'b000, control_1_signextend__0}
  IF_ID if_id_1 (
    .Instruction(rom_1_data), .Instruction_2(if_id_1_instruction_2), .PC_1(PC1), .PC_1_2(PC2), .enable(1'b1),
    .Clock(CLK), .Clear(clr));
  IR ir_1 (
    .opcode(op), .Rs(ir_1_rs), .Rt(ir_1_rt), .Rd(Rd), .funct(funct), .Input(if_id_1_instruction_2),
    .jAddr(jAddr), .offset(imm), .imm(imm));  // open: shamt
  Hex_Digit_Display hex_digit_display_6 (.value(d0[3:0]));  // open: dp
  Hex_Digit_Display hex_digit_display_7 (.value(d1[3:0]));  // open: dp
  Hex_Digit_Display hex_digit_display_8 (.value(d1[7:4]));  // open: dp
  // Probe on mem_wr_1_regdst_2
  // Probe on multiplexer_8_out
  // Probe on ir_1_rs
  // Probe on PC2
  // Probe on PC1
  // Probe on rg1
  // Probe on rg0
  // Probe on R_rt
  // Probe on R_rs
  not not_2 (not_2_out, CLK);
  assign controlled_buffer_1_out = not_2_out ? multiplexer_8_out : 16'bz;  // Controlled_Buffer controlled_buffer_1
  // Probe on PC3
  // Probe on rg3
  // Probe on rg2
  // Probe on RAMValue
  RF rf_1 (
    .Read_register_1(ir_1_rs), .Read_register_2(ir_1_rt), .write_register(mem_wr_1_regdst_2),
    .write_data(controlled_buffer_1_out), .Read_Data_1(R_rs), .Read_Data_2(R_rt), .Reg_0_Value(rg0),
    .Reg_1_Value(rg1), .Reg_2_Value(rg2), .Reg_3_Value(rg3), .RegWrite(RegWrite), .clock(CLK));
  // Probe on PC5
  // Probe on PC4
  // Probe on CLKCounter
  ID_EX id_ex_1 (
    .enable(1'b1), .Control(Control), .clock(CLK), .RD1(R_rs), .RD2(R_rt), .Rd(Rd), .clear(clr),
    .RD1_2(id_ex_1_rd1_2), .RD2_2(id_ex_1_rd2_2), .Rd_2(id_ex_1_rd_2), .Pc_4_2(PC3), .pc_4(PC2),
    .Control_2(id_ex_1_control_2), .imm_offset(imm), .imm_offset_2(id_ex_1_imm_offset_2), .jAddr(jAddr),
    .jAddr_2(id_ex_1_jaddr_2), .Rt(ir_1_rt), .Rt_2(id_ex_1_rt_2), .ALUOp(ALUOp), .ALUOp_2(id_ex_1_aluop_2),
    .Rs(ir_1_rs), .Rs_2(id_ex_1_rs_2));
  SignExtend signextend_1 (
    .imm_offset(id_ex_1_imm_offset_2), .extendOp(id_ex_1_control_2[0]),
    .extended_imm_offset(signextend_1_extended_imm_offset));
  Load_useControl load_usecontrol_1 (
    .ID_EX_MemRead(id_ex_1_control_2[8]), .ID_EX_Rt(id_ex_1_rt_2), .IF_ID_Rs(ir_1_rs), .IF_ID_Rt(ir_1_rt),
    .load_use(load_use));
  Multiplexer #(.width(2), .enable("false")) multiplexer_4 (
    .in0(id_ex_1_rt_2), .in1(id_ex_1_rd_2), .out(multiplexer_4_out), .sel(id_ex_1_control_2[1]));
  Adder #(.width(16)) adder_2 (.a(PC3), .b(signextend_1_extended_imm_offset), .out(adder_2_out));  // open: cin, cout
  Multiplexer #(.width(16), .enable("false")) multiplexer_5 (
    .in0(id_ex_1_rd2_2), .in1(signextend_1_extended_imm_offset), .out(multiplexer_5_out),
    .sel(id_ex_1_control_2[2]));
  // Probe on Forword1
  // Probe on Forword2
  Multiplexer #(.select(2), .width(16), .enable("false")) multiplexer_6 (
    .in0(id_ex_1_rd1_2), .in1(multiplexer_8_out), .in2(ex_mem_1_aluout_2), .out(multiplexer_6_out),
    .sel(Forword1));  // open: in3
  Multiplexer #(.select(2), .width(16), .enable("false")) multiplexer_7 (
    .in0(multiplexer_5_out), .in1(multiplexer_8_out), .in2(ex_mem_1_aluout_2), .out(multiplexer_7_out),
    .sel(Forword2));  // open: in3
  DataHazardsControl datahazardscontrol_1 (
    .EX_MEM_Rd(Ex_Mem_Rd), .MEM_WB_Rd(mem_wr_1_regdst_2), .ID_EX_Rs(id_ex_1_rs_2), .ID_EX_Rt(id_ex_1_rt_2),
    .EX_RegWrite(ex_mem_1_control_2[7]), .Mem_RegWrite(RegWrite), .Forward1(Forword1), .Forward2(Forword2));
  ALU alu_1 (
    .in_1(multiplexer_6_out), .in_2(multiplexer_7_out), .Sel(id_ex_1_aluop_2), .ALUOut(alu_1_aluout),
    .equal(alu_1_equal), .gt(alu_1_gt));  // open: zero, carry, Overflow
  EX_Mem ex_mem_1 (
    .enable(1'b1), .Control(id_ex_1_control_2[15:3]), .clock(CLK), .equal(alu_1_equal), .gt(alu_1_gt),
    .BranchAddr(adder_2_out), .aluout(alu_1_aluout), .Control_2({ex_mem_1_control_2, PCSrc[1]}), .clear(clr),
    .equal_2(ex_mem_1_equal_2), .gt_2(ex_mem_1_gt_2), .BranchAddr_2(BranchAddr),
    .aluout_2(ex_mem_1_aluout_2), .RegDst(multiplexer_4_out), .RegDst_2(Ex_Mem_Rd), .RD2(id_ex_1_rd2_2),
    .RD2_2(ex_mem_1_rd2_2), .PC(PC3), .PC_2(PC4), .jAddr_2(JumpAddr), .jAddr({PC3[15:12], id_ex_1_jaddr_2}));
  Branch branch_1 (
    .beq(ex_mem_1_control_2[1]), .ALU_beq(ex_mem_1_equal_2), .bnq(ex_mem_1_control_2[2]),
    .bgt(ex_mem_1_control_2[3]), .ALU_bgt(ex_mem_1_gt_2), .PCSrc(PCSrc[0]));
  assign controlled_buffer_2_out = ex_mem_1_control_2[4] ? ex_mem_1_rd2_2 : 16'bz;  // Controlled_Buffer controlled_buffer_2
  RAM #(.addrWidth(16), .dataWidth(16), .bus("separate")) ram_1 (
    .addr(ex_mem_1_aluout_2), .din(controlled_buffer_2_out), .data(RAMValue), .str(ex_mem_1_control_2[4]),
    .sel(1'b1), .clk(CLK), .ld(ex_mem_1_control_2[5]), .clr(clr));
  // Probe on ex_mem_1_aluout_2
  Mem_Wr mem_wr_1 (
    .enable(1'b1), .Control(ex_mem_1_control_2[12:6]), .clock(CLK), .ALUOut(ex_mem_1_aluout_2),
    .MemOut(RAMValue), .RegDst(Ex_Mem_Rd),
    .Control_2({mem_wr_1_control_2[6:4], Halt, display, RegWrite, mem_wr_1_control_2[0]}), .clear(clr),
    .ALUOut_2(mem_wr_1_aluout_2), .MemOut_2(mem_wr_1_memout_2), .RegDst_2(mem_wr_1_regdst_2), .PC(PC4),
    .PC_2(PC5));
  // Probe on multiplexer_8_out
  Multiplexer #(.width(16), .enable("false")) multiplexer_8 (
    .in0(mem_wr_1_aluout_2), .in1(mem_wr_1_memout_2), .out(multiplexer_8_out), .sel(mem_wr_1_control_2[0]));

  // Notes on the sheet:
  //   PC
  //   contents of rom_1 (hex, n*v repeats v):
  //   4*2 0 82 4*0 7300 45ff a1f7 8010 0 0 4001 2100 350f a1f0 c000
  //   sign extend
  //   ALUSrc
  //   Mem2Reg
endmodule

module RF (
  input  [1:0] Read_register_1,
  input  [1:0] Read_register_2,
  input  [1:0] write_register,
  input  [15:0] write_data,
  input  RegWrite,
  input  clock,
  output [15:0] Reg_0_Value,
  output [15:0] Reg_1_Value,
  output [15:0] Reg_2_Value,
  output [15:0] Reg_3_Value,
  output [15:0] Read_Data_1,
  output [15:0] Read_Data_2
);

  wire [15:0] multiplexer_1_out, multiplexer_2_out, multiplexer_3_out, multiplexer_4_out;

  Multiplexer #(.select(3), .width(16), .enable("false")) multiplexer_1 (
    .in0(Reg_0_Value), .in1(Reg_0_Value), .in2(Reg_0_Value), .in3(Reg_0_Value), .in4(write_data),
    .in5(Reg_0_Value), .in6(Reg_0_Value), .in7(Reg_0_Value), .out(multiplexer_1_out),
    .sel({RegWrite, write_register}));
  Register #(.width(16)) register_1 (.D(multiplexer_1_out), .en(1'b1), .Q(Reg_0_Value), .clk(clock), .clr(1'b0));
  Register #(.width(16)) register_2 (.D(multiplexer_2_out), .en(1'b1), .Q(Reg_1_Value), .clk(clock), .clr(1'b0));
  Multiplexer #(.select(3), .width(16), .enable("false")) multiplexer_2 (
    .in0(Reg_1_Value), .in1(Reg_1_Value), .in2(Reg_1_Value), .in3(Reg_1_Value), .in4(Reg_1_Value),
    .in5(write_data), .in6(Reg_1_Value), .in7(Reg_1_Value), .out(multiplexer_2_out),
    .sel({RegWrite, write_register}));
  Register #(.width(16)) register_3 (.D(multiplexer_3_out), .en(1'b1), .Q(Reg_2_Value), .clk(clock), .clr(1'b0));
  Multiplexer #(.select(3), .width(16), .enable("false")) multiplexer_3 (
    .in0(Reg_2_Value), .in1(Reg_2_Value), .in2(Reg_2_Value), .in3(Reg_2_Value), .in4(Reg_2_Value),
    .in5(Reg_2_Value), .in6(write_data), .in7(Reg_2_Value), .out(multiplexer_3_out),
    .sel({RegWrite, write_register}));
  Multiplexer #(.select(3), .width(16), .enable("false")) multiplexer_4 (
    .in0(Reg_3_Value), .in1(Reg_3_Value), .in2(Reg_3_Value), .in3(Reg_3_Value), .in4(Reg_3_Value),
    .in5(Reg_3_Value), .in6(Reg_3_Value), .in7(write_data), .out(multiplexer_4_out),
    .sel({RegWrite, write_register}));
  Register #(.width(16)) register_4 (.D(multiplexer_4_out), .en(1'b1), .Q(Reg_3_Value), .clk(clock), .clr(1'b0));
  Multiplexer #(.select(2), .width(16), .enable("false")) multiplexer_5 (
    .in0(Reg_0_Value), .in1(Reg_1_Value), .in2(Reg_2_Value), .in3(Reg_3_Value), .out(Read_Data_1),
    .sel(Read_register_1));
  Multiplexer #(.select(2), .width(16), .enable("false")) multiplexer_6 (
    .in0(Reg_0_Value), .in1(Reg_1_Value), .in2(Reg_2_Value), .in3(Reg_3_Value), .out(Read_Data_2),
    .sel(Read_register_2));

  // Notes on the sheet:
  //   INPUTS
  //   These are INPUTS to the circuit
  //   OUTPUTS
endmodule

module IR (
  input  [15:0] Input,
  output [3:0] opcode,
  output [1:0] Rs,
  output [1:0] Rt,
  output [1:0] Rd,
  output [2:0] shamt,
  output [2:0] funct,
  output [11:0] jAddr,
  output [7:0] offset,
  output [7:0] imm
);


  assign funct = Input[2:0];
  assign imm = Input[7:0];
  assign jAddr = Input[11:0];
  assign offset = Input[7:0];
  assign opcode = Input[15:12];
  assign Rd = Input[7:6];
  assign Rs = Input[11:10];
  assign Rt = Input[9:8];
  assign shamt = Input[5:3];

  // Other names for the same wires on the sheet: op[3:0] = Input[15:12]

  // Notes on the sheet:
  //   From IM
  //   Outputs
endmodule

module ALU (
  input  [15:0] in_1,
  input  [15:0] in_2,
  input  [3:0] Sel,
  output carry,
  output Overflow,
  output gt,
  output equal,
  output [15:0] ALUOut,
  output zero
);

  wire adder_1_cout, and_2_out, and_3_out, and_4_out, and_5_out, comparator_1_lt, not_1_out, not_2_out,
       not_3_out, not_4_out, or_2_out, or_3_out, subtractor_1_bout;
  wire [15:0] adder_1_out, adder_2_out, and_out, bit_extender_1_out, OR_out, shifter_1_out, shifter_2_out,
       shifter_3_out, shifter_4_out, subtractor_1_out, XOR_out;

  Comparator #(.width(16)) comparator_1 (.a(in_1), .b(in_2), .gt(gt), .eq(equal), .lt(comparator_1_lt));
  Shifter #(.width(16)) shifter_1 (.in(in_2), .\dist (4'b1000), .out(shifter_1_out));
  Adder #(.width(16)) adder_1 (.a(in_1), .b(in_2), .out(adder_1_out), .cin(1'b0), .cout(adder_1_cout));
  Subtractor #(.width(16)) subtractor_1 (
    .a(in_1), .b(in_2), .out(subtractor_1_out), .bin(1'b0), .bout(subtractor_1_bout));
  assign and_out = in_1 & in_2;  // AND_Gate and, 16 bits wide
  not not_1 (not_1_out, subtractor_1_out[15]);
  assign bit_extender_1_out = {{15{1'b0}}, comparator_1_lt};  // Bit_Extender bit_extender_1
  assign OR_out = in_1 | in_2;  // OR_Gate OR, 16 bits wide
  assign XOR_out = in_1 ^ in_2;  // XOR_Gate XOR, 16 bits wide
  Shifter #(.width(16)) shifter_2 (.in(in_1), .\dist (in_2[3:0]), .out(shifter_2_out));
  Shifter #(.width(16), .shift("lr")) shifter_3 (.in(in_1), .\dist (in_2[3:0]), .out(shifter_3_out));
  Shifter #(.width(16), .shift("ar")) shifter_4 (.in(in_1), .\dist (in_2[3:0]), .out(shifter_4_out));
  not not_2 (not_2_out, in_1[15]);
  and and_2 (and_2_out, in_1[15], in_2[15], not_1_out);
  Adder #(.width(16)) adder_2 (.a(adder_1_out), .b(16'h1), .out(adder_2_out));  // open: cin, cout
  not not_3 (not_3_out, in_2[15]);
  not not_4 (not_4_out, adder_1_out[15]);
  and and_3 (and_3_out, not_3_out, not_2_out, subtractor_1_out[15]);
  Multiplexer #(.select(4), .width(16)) multiplexer_1 (
    .in0(OR_out), .in1(and_out), .in2(adder_2_out), .in3(subtractor_1_out), .in4(shifter_2_out),
    .in5(shifter_3_out), .in6(shifter_4_out), .in7(bit_extender_1_out), .in8(shifter_1_out), .out(ALUOut),
    .sel(Sel), .en(1'b1));  // open: in9, in10, in11, in12, in13, in14, in15
  and and_4 (and_4_out, not_2_out, not_3_out, adder_1_out[15]);
  and and_5 (and_5_out, in_1[15], in_2[15], not_4_out);
  or or_2 (or_2_out, and_2_out, and_3_out);
  or or_3 (or_3_out, and_4_out, and_5_out);
  Multiplexer #(.select(2)) multiplexer_2 (
    .in0(adder_1_cout), .in1(subtractor_1_bout), .out(carry), .sel(Sel[1:0]), .en(1'b1));  // open: in2, in3
  nor nor_1 (zero, ALUOut[0], ALUOut[1], ALUOut[2], ALUOut[3], ALUOut[4], ALUOut[5], ALUOut[6], ALUOut[7], ALUOut[8], ALUOut[9], ALUOut[10], ALUOut[11], ALUOut[12], ALUOut[13], ALUOut[14], ALUOut[15]);
  Multiplexer #(.select(2)) multiplexer_3 (
    .in0(or_3_out), .in1(or_2_out), .out(Overflow), .sel(Sel[1:0]), .en(1'b1));  // open: in2, in3

  // Notes on the sheet:
  //   A
  //   B
  //   Lui
endmodule

module Control (
  input  [3:0] op,
  input  [2:0] func,
  output [15:0] Control,
  output regWrite_10,
  output signExtend__0,
  output RegDst_1,
  output aluSource_2,
  output memToReg_9,
  output memWrite_7,
  output memRead_8,
  output display_11,
  output Jump_3,
  output beq_4,
  output bne_5,
  output bgt_6,
  output halt_12,
  output [3:0] aluFunc
);

  wire [3:0] bit_extender_1_out;

  Multiplexer #(.select(4), .enable("false")) multiplexer_1 (
    .in0(1'b1), .in1(1'b0), .in2(1'b1), .in3(1'b1), .in4(1'b1), .in5(1'b1), .in6(1'b1), .in7(1'b0),
    .in8(1'b0), .in9(1'b0), .in10(1'b0), .in11(1'b0), .in12(1'b0), .in13(1'b0), .in14(1'b0), .in15(1'b0),
    .out(Control[10]), .sel(op));
  assign bit_extender_1_out = {{1{1'b0}}, func};  // Bit_Extender bit_extender_1
  Multiplexer #(.select(4), .enable("false")) multiplexer_2 (
    .in0(1'b0), .in1(1'b0), .in2(1'b0), .in3(1'b0), .in4(1'b1), .in5(1'b0), .in6(1'b1), .in7(1'b1),
    .in8(1'b0), .in9(1'b1), .in10(1'b1), .in11(1'b1), .in12(1'b0), .in13(1'b0), .in14(1'b0), .in15(1'b0),
    .out(Control[0]), .sel(op));
  Multiplexer #(.select(4), .enable("false")) multiplexer_3 (
    .in0(1'b1), .in2(1'b0), .in3(1'b0), .in4(1'b0), .in5(1'b0), .in6(1'b0), .in7(1'b0), .in8(1'b0),
    .in9(1'b0), .in10(1'b0), .in11(1'b0), .in12(1'b0), .in13(1'b0), .in14(1'b0), .in15(1'b0),
    .out(Control[1]), .sel(op));  // open: in1
  Multiplexer #(.select(4), .width(4), .enable("false")) multiplexer_4 (
    .in0(bit_extender_1_out), .in2(4'b1000), .in3(4'b0000), .in4(4'b0010), .in5(4'b0001), .in6(4'b0010),
    .in7(4'b0010), .out(aluFunc), .sel(op));  // open: in1, in8, in9, in10, in11, in12, in13, in14, in15
  Multiplexer #(.select(4), .enable("false")) multiplexer_5 (
    .in0(1'b0), .in1(1'b1), .in2(1'b1), .in3(1'b1), .in4(1'b1), .in5(1'b1), .in6(1'b1), .in7(1'b1),
    .in8(1'b0), .in9(1'b0), .in10(1'b0), .in11(1'b0), .in12(1'b1), .in13(1'b1), .in14(1'b1), .in15(1'b1),
    .out(aluSource_2), .sel(op));
  Multiplexer #(.select(4), .enable("false")) multiplexer_6 (
    .in0(1'b0), .in2(1'b0), .in3(1'b0), .in4(1'b0), .in5(1'b0), .in6(1'b1), .in7(1'b0), .in8(1'b0),
    .in9(1'b0), .in10(1'b0), .in11(1'b0), .in12(1'b0), .in13(1'b0), .in14(1'b0), .in15(1'b0),
    .out(Control[9]), .sel(op));  // open: in1
  Multiplexer #(.select(4), .enable("false")) multiplexer_7 (
    .in0(1'b0), .in1(1'b0), .in2(1'b0), .in3(1'b0), .in4(1'b0), .in5(1'b0), .in6(1'b0), .in7(1'b1),
    .in8(1'b0), .in9(1'b0), .in10(1'b0), .in11(1'b0), .in12(1'b0), .in13(1'b0), .in14(1'b0), .in15(1'b0),
    .out(Control[7]), .sel(op));
  Multiplexer #(.select(4), .enable("false")) multiplexer_8 (
    .in0(1'b0), .in1(1'b0), .in2(1'b0), .in3(1'b0), .in4(1'b0), .in5(1'b0), .in6(1'b1), .in7(1'b0),
    .in8(1'b0), .in9(1'b0), .in10(1'b0), .in11(1'b0), .in12(1'b0), .in13(1'b0), .in14(1'b0), .in15(1'b0),
    .out(Control[8]), .sel(op));
  Multiplexer #(.select(4), .enable("false")) multiplexer_9 (
    .in0(1'b0), .in1(1'b1), .in2(1'b0), .in3(1'b0), .in4(1'b0), .in5(1'b0), .in6(1'b0), .in7(1'b0),
    .in8(1'b0), .in9(1'b0), .in10(1'b0), .in11(1'b0), .in12(1'b0), .in13(1'b0), .in14(1'b0), .in15(1'b0),
    .out(Control[11]), .sel(op));
  Comparator #(.width(4)) comparator_1 (.a(op), .b(4'b1000), .eq(Control[3]));  // open: gt, lt
  Comparator #(.width(4)) comparator_2 (.a(op), .b(4'b1001), .eq(beq_4));  // open: gt, lt
  Comparator #(.width(4)) comparator_3 (.a(op), .b(4'b1010), .eq(bne_5));  // open: gt, lt
  Comparator #(.width(4)) comparator_4 (.a(op), .b(4'b1011), .eq(bgt_6));  // open: gt, lt
  Comparator #(.width(4)) comparator_5 (.a(op), .b(4'b1100), .eq(Control[12]));  // open: gt, lt

  assign {Control[15:13], Control[6:4], Control[2]} = {3'b000, bgt_6, bne_5, beq_4, aluSource_2};
  assign display_11 = Control[11];
  assign halt_12 = Control[12];
  assign Jump_3 = Control[3];
  assign memRead_8 = Control[8];
  assign memToReg_9 = Control[9];
  assign memWrite_7 = Control[7];
  assign RegDst_1 = Control[1];
  assign regWrite_10 = Control[10];
  assign signExtend__0 = Control[0];
endmodule

module SignExtend (
  input  [7:0] imm_offset,
  input  extendOp,
  output [15:0] extended_imm_offset
);

  wire [15:0] bit_extender_1_out, bit_extender_2_out;

  assign bit_extender_1_out = {{8{1'b0}}, imm_offset};  // Bit_Extender bit_extender_1
  assign bit_extender_2_out = {{8{imm_offset[7]}}, imm_offset};  // Bit_Extender bit_extender_2
  Multiplexer #(.width(16), .enable("false")) multiplexer_1 (
    .in0(bit_extender_1_out), .in1(bit_extender_2_out), .out(extended_imm_offset), .sel(extendOp));
endmodule

module Branch (
  input  beq,
  input  ALU_beq,
  input  bnq,
  input  bgt,
  input  ALU_bgt,
  output PCSrc
);

  wire and_1_out, and_2_out, and_3_out, not_1_out;

  not not_1 (not_1_out, ALU_beq);
  and and_1 (and_1_out, beq, ALU_beq);
  and and_2 (and_2_out, bnq, not_1_out);
  and and_3 (and_3_out, bgt, ALU_bgt);
  or or_1 (PCSrc, and_1_out, and_2_out, and_3_out);
endmodule

module IF_ID (
  input  enable,
  input  [15:0] PC_1,
  input  Clock,
  input  [15:0] Instruction,
  input  Clear,
  output [15:0] PC_1_2,
  output [15:0] Instruction_2
);

  wire register_3_q, reset;

  Register #(.width(16)) register_1 (.D(PC_1), .en(enable), .Q(PC_1_2), .clk(Clock), .clr(reset));
  Register #(.width(16)) register_2 (.D(Instruction), .en(enable), .Q(Instruction_2), .clk(Clock), .clr(reset));
  Register #(.width(1)) register_3 (.D(1'b1), .en(enable), .Q(register_3_q), .clk(Clock), .clr(reset));
  and and_1 (reset, Clear, register_3_q);

  // Other names for the same wires on the sheet: en = enable
endmodule

module ID_EX (
  input  enable,
  input  [15:0] Control,
  input  clock,
  input  clear,
  input  [3:0] ALUOp,
  input  [15:0] RD1,
  input  [15:0] RD2,
  input  [1:0] Rt,
  input  [1:0] Rd,
  input  [15:0] pc_4,
  input  [7:0] imm_offset,
  input  [11:0] jAddr,
  input  [1:0] Rs,
  output [15:0] Control_2,
  output [3:0] ALUOp_2,
  output [15:0] RD1_2,
  output [15:0] RD2_2,
  output [1:0] Rt_2,
  output [1:0] Rd_2,
  output [15:0] Pc_4_2,
  output [7:0] imm_offset_2,
  output [11:0] jAddr_2,
  output [1:0] Rs_2
);

  Register #(.width(16)) register_1 (.D(Control), .en(enable), .Q(Control_2), .clk(clock), .clr(clear));
  Register #(.width(4)) register_2 (.D(ALUOp), .en(enable), .Q(ALUOp_2), .clk(clock), .clr(clear));
  Register #(.width(16)) register_3 (.D(RD1), .en(enable), .Q(RD1_2), .clk(clock), .clr(clear));
  Register #(.width(16)) register_4 (.D(RD2), .en(enable), .Q(RD2_2), .clk(clock), .clr(clear));
  Register #(.width(2)) register_5 (.D(Rt), .en(enable), .Q(Rt_2), .clk(clock), .clr(clear));
  Register #(.width(2)) register_6 (.D(Rd), .en(enable), .Q(Rd_2), .clk(clock), .clr(clear));
  Register #(.width(16)) register_7 (.D(pc_4), .en(enable), .Q(Pc_4_2), .clk(clock), .clr(clear));
  Register register_8 (.D(imm_offset), .en(enable), .Q(imm_offset_2), .clk(clock), .clr(clear));
  Register #(.width(12)) register_9 (.D(jAddr), .en(enable), .Q(jAddr_2), .clk(clock), .clr(clear));
  Register #(.width(2)) register_10 (.D(Rs), .en(enable), .Q(Rs_2), .clk(clock), .clr(clear));
endmodule

module EX_Mem (
  input  enable,
  input  [12:0] Control,
  input  clock,
  input  clear,
  input  equal,
  input  gt,
  input  [15:0] BranchAddr,
  input  [15:0] aluout,
  input  [1:0] RegDst,
  input  [15:0] RD2,
  input  [15:0] PC,
  input  [15:0] jAddr,
  output [12:0] Control_2,
  output equal_2,
  output gt_2,
  output [15:0] BranchAddr_2,
  output [15:0] aluout_2,
  output [1:0] RegDst_2,
  output [15:0] RD2_2,
  output [15:0] PC_2,
  output [15:0] jAddr_2
);

  Register #(.width(13)) register_1 (.D(Control), .en(enable), .Q(Control_2), .clk(clock), .clr(clear));
  Register #(.width(1)) register_2 (.D(equal), .en(enable), .Q(equal_2), .clk(clock), .clr(clear));
  Register #(.width(1)) register_3 (.D(gt), .en(enable), .Q(gt_2), .clk(clock), .clr(clear));
  Register #(.width(16)) register_4 (.D(BranchAddr), .en(enable), .Q(BranchAddr_2), .clk(clock), .clr(clear));
  Register #(.width(16)) register_5 (.D(aluout), .en(enable), .Q(aluout_2), .clk(clock), .clr(clear));
  Register #(.width(2)) register_6 (.D(RegDst), .en(enable), .Q(RegDst_2), .clk(clock), .clr(clear));
  Register #(.width(16)) register_7 (.D(RD2), .en(enable), .Q(RD2_2), .clk(clock), .clr(clear));
  Register #(.width(16)) register_8 (.D(PC), .en(enable), .Q(PC_2), .clk(clock), .clr(clear));
  Register #(.width(16)) register_9 (.D(jAddr), .en(enable), .Q(jAddr_2), .clk(clock), .clr(clear));
endmodule

module Mem_Wr (
  input  enable,
  input  [6:0] Control,
  input  clock,
  input  clear,
  input  [15:0] ALUOut,
  input  [15:0] MemOut,
  input  [1:0] RegDst,
  input  [15:0] PC,
  output [6:0] Control_2,
  output [15:0] ALUOut_2,
  output [15:0] MemOut_2,
  output [1:0] RegDst_2,
  output [15:0] PC_2
);

  Register #(.width(7)) register_1 (.D(Control), .en(enable), .Q(Control_2), .clk(clock), .clr(clear));
  Register #(.width(16)) register_2 (.D(ALUOut), .en(enable), .Q(ALUOut_2), .clk(clock), .clr(clear));
  Register #(.width(16)) register_3 (.D(MemOut), .en(enable), .Q(MemOut_2), .clk(clock), .clr(clear));
  Register #(.width(2)) register_4 (.D(RegDst), .en(enable), .Q(RegDst_2), .clk(clock), .clr(clear));
  Register #(.width(16)) register_5 (.D(PC), .en(enable), .Q(PC_2), .clk(clock), .clr(clear));
endmodule

// DataHazards
module DataHazardsControl (
  input  EX_RegWrite,
  input  Mem_RegWrite,
  input  [1:0] EX_MEM_Rd,
  input  [1:0] MEM_WB_Rd,
  input  [1:0] ID_EX_Rs,
  input  [1:0] ID_EX_Rt,
  output [1:0] Forward1,
  output [1:0] Forward2
);

  wire comparator_1_eq, comparator_2_eq, comparator_3_eq, comparator_4_eq;
  wire [1:0] and_3_out, and_4_out, multiplexer_1_out, multiplexer_2_out, multiplexer_3_out,
       multiplexer_4_out, multiplexer_5_out, multiplexer_6_out;

  Comparator #(.width(2)) comparator_1 (.a(EX_MEM_Rd), .b(ID_EX_Rs), .eq(comparator_1_eq));  // open: gt, lt
  Comparator #(.width(2)) comparator_2 (.a(EX_MEM_Rd), .b(ID_EX_Rt), .eq(comparator_2_eq));  // open: gt, lt
  Comparator #(.width(2)) comparator_3 (.a(MEM_WB_Rd), .b(ID_EX_Rs), .eq(comparator_3_eq));  // open: gt, lt
  Comparator #(.width(2)) comparator_4 (.a(MEM_WB_Rd), .b(ID_EX_Rt), .eq(comparator_4_eq));  // open: gt, lt
  and and_1 (and_3_out[1], EX_RegWrite, comparator_1_eq);
  Multiplexer #(.width(2), .enable("false")) multiplexer_1 (
    .in0(2'b00), .in1(2'b10), .out(multiplexer_1_out), .sel(and_3_out[1]));
  and and_2 (and_4_out[1], EX_RegWrite, comparator_2_eq);
  and and_3 (and_3_out[0], Mem_RegWrite, comparator_3_eq);
  and and_4 (and_4_out[0], Mem_RegWrite, comparator_4_eq);
  Multiplexer #(.width(2), .enable("false")) multiplexer_2 (
    .in0(2'b00), .in1(2'b01), .out(multiplexer_2_out), .sel(and_3_out[0]));
  Multiplexer #(.width(2), .enable("false")) multiplexer_3 (
    .in0(2'b00), .in1(2'b10), .out(multiplexer_3_out), .sel(and_4_out[1]));
  Multiplexer #(.width(2), .enable("false")) multiplexer_4 (
    .in0(2'b00), .in1(2'b01), .out(multiplexer_4_out), .sel(and_4_out[0]));
  Multiplexer #(.select(2), .width(2), .enable("false")) multiplexer_5 (
    .in0(2'b00), .in1(2'b01), .in2(2'b10), .in3(2'b10), .out(multiplexer_5_out), .sel(and_3_out));
  Multiplexer #(.select(2), .width(2), .enable("false")) multiplexer_6 (
    .in0(2'b00), .in1(2'b01), .in2(2'b10), .in3(2'b10), .out(multiplexer_6_out), .sel(and_4_out));
  Multiplexer #(.select(2), .width(2), .enable("false")) multiplexer_7 (
    .in0(2'b00), .in1(multiplexer_2_out), .in2(multiplexer_1_out), .in3(multiplexer_5_out), .out(Forward1),
    .sel({EX_RegWrite, Mem_RegWrite}));
  Multiplexer #(.select(2), .width(2), .enable("false")) multiplexer_8 (
    .in0(2'b00), .in1(multiplexer_4_out), .in2(multiplexer_3_out), .in3(multiplexer_6_out), .out(Forward2),
    .sel({EX_RegWrite, Mem_RegWrite}));

  // Notes on the sheet:
  //   high
endmodule

module Load_useControl (
  input  ID_EX_MemRead,
  input  [1:0] ID_EX_Rt,
  input  [1:0] IF_ID_Rs,
  input  [1:0] IF_ID_Rt,
  output load_use
);

  wire comparator_1_eq, comparator_2_eq, or_1_out;

  Comparator #(.width(2)) comparator_1 (.a(ID_EX_Rt), .b(IF_ID_Rs), .eq(comparator_1_eq));  // open: gt, lt
  Comparator #(.width(2)) comparator_2 (.a(ID_EX_Rt), .b(IF_ID_Rt), .eq(comparator_2_eq));  // open: gt, lt
  or or_1 (or_1_out, comparator_1_eq, comparator_2_eq);
  and and_1 (load_use, ID_EX_MemRead, or_1_out);
endmodule
